# Fritzing sketch schematic (saved by Fritzing 0.9.3b)
breadboards: 1

parts:
  Part1 = Arduino Uno (Rev3)
  R1 = Resistor [tolerance=±5% resistance=220 package=THT]
  R2 = Resistor [tolerance=±5% resistance=220 package=THT]
  R3 = Resistor [tolerance=±5% resistance=220 package=THT]
  LED1 = LED - 5mm [color="Green (560nm)" package="5 mm [THT]"]
  LED2 = LED - 5mm [color="Green (560nm)" package="5 mm [THT]"]
  LED3 = LED - 5mm [color="Green (560nm)" package="5 mm [THT]"]
  R4 = Resistor [tolerance=±5% resistance=100 package=THT]
  S1 = Pushbutton [package="[THT]"]

nets:
  N1: Part1.D10_PWM/SS, R2.Pin_0
  N2: Part1.D11_PWM/MOSI, R3.Pin_0
  N3: Part1.D12/MISO, R1.Pin_0
  N4: Part1.D13/SCK, R4.Pin_0, S1.Pin_3, S1.Pin_4
  N5: Part1.5V, R4.Pin_1
  N6: Part1.GND, LED1.anode, LED2.anode, LED3.anode, S1.Pin_1, S1.Pin_2
  N7: R1.Pin_1, LED1.cathode
  N8: R2.Pin_1, LED2.cathode
  N9: R3.Pin_1, LED3.cathode
